// Logisim project Progetto Laboratorio .circ as structural Verilog: 13 circuits, main circuit Circuito Principale
module Interfaccia_Utente (
);

  wire A_out, circuito_principale_1_setting_completo, clock_1_out, E_out, F_out, I_out, L_out, O_out, R1_out,
       R2_out, R3_out, Reset_out, S_out, Set_Iniziale_Concluso_out;
  wire [2:0] L__da_Sost__1, L__da_Sost__2, L__in_Sost__1, L__in_Sost__2, Lettera_al_PlugBoard,
       Lettera_Finale, Pos_R_1, Pos_R_2, Pos_R_3, Ultima_Lettera_Inserita;
  wire [3:0] bit_extender_1_out, bit_extender_2_out, bit_extender_3_out;
  wire [7:0] convertitore_led_1_out_2, convertitore_led_2_out_2, convertitore_led_3_out_2,
       convertitore_led_4_out_2, convertitore_led_5_out_2, convertitore_led_6_out_2, convertitore_led_7_out_2;

  Hex_Digit_Display hex_digit_display_1 (.value(bit_extender_1_out));  // open: dp
  assign bit_extender_1_out = {{1{1'b0}}, Pos_R_1};  // Bit_Extender bit_extender_1
  assign bit_extender_2_out = {{1{1'b0}}, Pos_R_2};  // Bit_Extender bit_extender_2
  assign bit_extender_3_out = {{1{1'b0}}, Pos_R_3};  // Bit_Extender bit_extender_3
  Convertitore_Led convertitore_led_1 (.out_2(convertitore_led_1_out_2), .in_1(L__da_Sost__1));
  Clock clock_1 (.out(clock_1_out));
  Button Reset (.out(Reset_out));
  Hex_Digit_Display hex_digit_display_2 (.value(bit_extender_3_out));  // open: dp
  Hex_Digit_Display hex_digit_display_3 (.value(bit_extender_2_out));  // open: dp
  _7_Segment_Display u_7_segment_display_1 (
    .g(convertitore_led_1_out_2[3]), .f(convertitore_led_1_out_2[2]), .a(convertitore_led_1_out_2[1]),
    .b(convertitore_led_1_out_2[0]), .e(convertitore_led_1_out_2[4]), .d(convertitore_led_1_out_2[5]),
    .c(convertitore_led_1_out_2[6]), .dp(convertitore_led_1_out_2[7]));
  LED led_1 (.in(circuito_principale_1_setting_completo));
  Button Set_Iniziale_Concluso (.out(Set_Iniziale_Concluso_out));
  Convertitore_Led convertitore_led_2 (.out_2(convertitore_led_2_out_2), .in_1(L__in_Sost__1));
  Button R2 (.out(R2_out));
  Button R3 (.out(R3_out));
  Button R1 (.out(R1_out));
  Convertitore_Led convertitore_led_3 (.out_2(convertitore_led_3_out_2), .in_1(Ultima_Lettera_Inserita));
  _7_Segment_Display u_7_segment_display_2 (
    .g(convertitore_led_2_out_2[3]), .f(convertitore_led_2_out_2[2]), .a(convertitore_led_2_out_2[1]),
    .b(convertitore_led_2_out_2[0]), .e(convertitore_led_2_out_2[4]), .d(convertitore_led_2_out_2[5]),
    .c(convertitore_led_2_out_2[6]), .dp(convertitore_led_2_out_2[7]));
  _7_Segment_Display u_7_segment_display_3 (
    .g(convertitore_led_3_out_2[3]), .f(convertitore_led_3_out_2[2]), .a(convertitore_led_3_out_2[1]),
    .b(convertitore_led_3_out_2[0]), .e(convertitore_led_3_out_2[4]), .d(convertitore_led_3_out_2[5]),
    .c(convertitore_led_3_out_2[6]), .dp(convertitore_led_3_out_2[7]));
  Button E (.out(E_out));
  Button A (.out(A_out));
  Convertitore_Led convertitore_led_4 (.out_2(convertitore_led_4_out_2), .in_1(L__da_Sost__2));
  Button I (.out(I_out));
  Button O (.out(O_out));
  Convertitore_Led convertitore_led_5 (.out_2(convertitore_led_5_out_2), .in_1(Lettera_al_PlugBoard));
  _7_Segment_Display u_7_segment_display_4 (
    .g(convertitore_led_4_out_2[3]), .f(convertitore_led_4_out_2[2]), .a(convertitore_led_4_out_2[1]),
    .b(convertitore_led_4_out_2[0]), .e(convertitore_led_4_out_2[4]), .d(convertitore_led_4_out_2[5]),
    .c(convertitore_led_4_out_2[6]), .dp(convertitore_led_4_out_2[7]));
  Circuito_Principale circuito_principale_1 (
    .Clock(clock_1_out), .Reset(Reset_out), .Setting_Completo(circuito_principale_1_setting_completo),
    .Lettera_Finale(Lettera_Finale), .Lettera_al_Plugboard(Lettera_al_PlugBoard),
    .Ultima_Lettera_Inserita(Ultima_Lettera_Inserita), .Posizione_R__1(Pos_R_1),
    .L__da_sost__1(L__da_Sost__1), .L__da_sost__2(L__da_Sost__2), .Posizione_R__2(Pos_R_2),
    .L__in_sost__1(L__in_Sost__1), .L__in_sost__2(L__in_Sost__2), .Posizione_R__3(Pos_R_3), .A(A_out),
    .E(E_out), .Pos__R__1(R1_out), .I(I_out), .O(O_out), .Pos__R__2(R2_out), .S(S_out), .F(F_out),
    .Pos__R__3(R3_out), .L(L_out), .Setting_Concluso(Set_Iniziale_Concluso_out));
  Button S (.out(S_out));
  Button F (.out(F_out));
  _7_Segment_Display u_7_segment_display_5 (
    .g(convertitore_led_5_out_2[3]), .f(convertitore_led_5_out_2[2]), .a(convertitore_led_5_out_2[1]),
    .b(convertitore_led_5_out_2[0]), .e(convertitore_led_5_out_2[4]), .d(convertitore_led_5_out_2[5]),
    .c(convertitore_led_5_out_2[6]), .dp(convertitore_led_5_out_2[7]));
  Button L (.out(L_out));
  Convertitore_Led convertitore_led_6 (.out_2(convertitore_led_6_out_2), .in_1(Lettera_Finale));
  Convertitore_Led convertitore_led_7 (.out_2(convertitore_led_7_out_2), .in_1(L__in_Sost__2));
  _7_Segment_Display u_7_segment_display_6 (
    .g(convertitore_led_6_out_2[3]), .f(convertitore_led_6_out_2[2]), .a(convertitore_led_6_out_2[1]),
    .b(convertitore_led_6_out_2[0]), .e(convertitore_led_6_out_2[4]), .d(convertitore_led_6_out_2[5]),
    .c(convertitore_led_6_out_2[6]), .dp(convertitore_led_6_out_2[7]));
  _7_Segment_Display u_7_segment_display_7 (
    .g(convertitore_led_7_out_2[3]), .f(convertitore_led_7_out_2[2]), .a(convertitore_led_7_out_2[1]),
    .b(convertitore_led_7_out_2[0]), .e(convertitore_led_7_out_2[4]), .d(convertitore_led_7_out_2[5]),
    .c(convertitore_led_7_out_2[6]), .dp(convertitore_led_7_out_2[7]));

  // Notes on the sheet:
  //   Posizioni Rotori
  //   Posizioni Rotori
endmodule

module Circuito_Principale (
  input  Clock,
  input  Reset,
  input  Setting_Concluso,
  input  A,
  input  E,
  input  I,
  input  O,
  input  S,
  input  F,
  input  L,
  input  Pos__R__1,
  input  Pos__R__2,
  input  Pos__R__3,
  output [2:0] Posizione_R__1,
  output [2:0] Posizione_R__2,
  output [2:0] Posizione_R__3,
  output [2:0] Lettera_Finale,
  output [2:0] Lettera_al_Plugboard,
  output [2:0] L__da_sost__1,
  output [2:0] L__in_sost__1,
  output [2:0] L__da_sost__2,
  output [2:0] L__in_sost__2,
  output [2:0] Ultima_Lettera_Inserita,
  output Setting_Completo
);

  wire Pulsante_Premuto;
  wire [2:0] demultiplexer_1_out0, demultiplexer_1_out1, pulsantiera_1_out_8;

  Memoria_Posizioni_Rotori memoria_posizioni_rotori_1 (
    .Reset(Reset), .Setting_Concluso(Setting_Completo), .Posizione_R_1(Posizione_R__1),
    .Posizione_R_2(Posizione_R__2), .Posizione_R_3(Posizione_R__3), .Input_Pos__1(Pos__R__1),
    .Input_Pos__2(Pos__R__2), .Input_Pos__3(Pos__R__3), .Clock(Clock), .Tastiera_Attivata(Pulsante_Premuto));
  Memoria_PlugBoard memoria_plugboard_1 (
    .Lettera_in_Input(demultiplexer_1_out0), .Reset(Reset), .Prima_Lettera_da_Sostituire(L__da_sost__1),
    .Prima_Lettera_in_Sostituzione(L__in_sost__1), .Seconda_Lettera_da_Sostituire(L__da_sost__2),
    .Seconda_Lettera_in_Sostituzione(L__in_sost__2), .Clock(Clock));
  S_R_Flip_Flop s_r_ff_1 (
    .S(Setting_Concluso), .clk(Clock), .R(Reset), .Q(Setting_Completo));  // open: Qn, preset, reset, en
  Demultiplexer #(.width(3)) demultiplexer_1 (
    .out0(demultiplexer_1_out0), .out1(demultiplexer_1_out1), .in(pulsantiera_1_out_8), .sel(Setting_Completo));  // open: en
  Rotori rotori_1 (
    .Lettera_in_Input(Lettera_al_Plugboard), .Lettera_in_Output(Lettera_Finale),
    .Posizione_Rotore_1(Posizione_R__1), .Posizione_Rotore_2(Posizione_R__2),
    .Posizione_Rotore_3(Posizione_R__3));
  PlugBoard plugboard_1 (
    .Lettera_in_Input(Ultima_Lettera_Inserita), .Output(Lettera_al_Plugboard),
    .Prima_Lettera_da_Sostituire(L__da_sost__1), .Seconda_Lettera_da_Sostituire(L__da_sost__2),
    .Prima_Lettera_in_Sostituzione(L__in_sost__1), .Seconda_Lettera_in_Sostituzione(L__in_sost__2));
  Ultima_Lettera_Inserita ultima_lettera_inserita_1 (
    .Lettera_in_Input(demultiplexer_1_out1), .Clock(Clock), .out_4(Ultima_Lettera_Inserita), .Reset(Reset));
  Pulsantiera pulsantiera_1 (
    .Pulsante_Premuto(Pulsante_Premuto), .out_8(pulsantiera_1_out_8), .in_1(A), .in_2(E), .in_3(I), .in_4(O),
    .in_5(S), .in_6(F), .in_7(L));

  // Other names for the same wires on the sheet: Input_R_1 = Pos__R__1; Input_R_2 = Pos__R__2; Input_R_3 = Pos__R__3

  // Notes on the sheet:
  //   Mem. Setting Completo
endmodule

// Mem. Rotori
module Memoria_Posizioni_Rotori (
  input  Reset,
  input  Setting_Concluso,
  input  Tastiera_Attivata,
  input  Clock,
  input  Input_Pos__1,
  input  Input_Pos__2,
  input  Input_Pos__3,
  output [2:0] Posizione_R_1,
  output [2:0] Posizione_R_2,
  output [2:0] Posizione_R_3
);

  wire _1_Scatto_R__1_Fatto_q, _1_Scatto_R__2_Fatto_q, and_1_out, and_2_out, multiplexer_1_out,
       multiplexer_2_out, multiplexer_3_out, or_1_out, or_2_out, or_3_out,
       verifica_posizione_rotore_1_da_ritornare_a_0, verifica_posizione_rotore_2_da_ritornare_a_0,
       verifica_posizione_rotore_3_da_ritornare_a_0;

  or or_1 (or_1_out, verifica_posizione_rotore_1_da_ritornare_a_0, Reset);
  Multiplexer multiplexer_1 (
    .in0(Input_Pos__1), .in1(Tastiera_Attivata), .out(multiplexer_1_out), .sel(Setting_Concluso));  // open: en
  S_R_Flip_Flop _1_Scatto_R__1_Fatto (
    .S(Posizione_R_1[0]), .clk(Clock), .R(Reset), .Q(_1_Scatto_R__1_Fatto_q));  // open: Qn, preset, reset, en
  Verifica_Posizione_Rotore verifica_posizione_rotore_1 (
    .in_1(Posizione_R_1), .Da_ritornare_a_0(verifica_posizione_rotore_1_da_ritornare_a_0));
  Counter #(.width(3), .max('h7)) counter_1 (
    .Q(Posizione_R_1), .clk(multiplexer_1_out), .clr(or_1_out));  // open: load, D, count, carry
  Verifica_Posizione_Rotore verifica_posizione_rotore_2 (
    .in_1(Posizione_R_2), .Da_ritornare_a_0(verifica_posizione_rotore_2_da_ritornare_a_0));
  Counter #(.width(3), .max('h7)) counter_2 (
    .Q(Posizione_R_2), .clk(multiplexer_2_out), .clr(or_2_out));  // open: load, D, count, carry
  or or_2 (or_2_out, verifica_posizione_rotore_2_da_ritornare_a_0, Reset);
  Multiplexer multiplexer_2 (
    .in0(Input_Pos__2), .in1(and_1_out), .out(multiplexer_2_out), .sel(Setting_Concluso));  // open: en
  and and_1 (and_1_out, verifica_posizione_rotore_1_da_ritornare_a_0, _1_Scatto_R__1_Fatto_q, Tastiera_Attivata);
  S_R_Flip_Flop _1_Scatto_R__2_Fatto (
    .S(Posizione_R_2[0]), .clk(Clock), .R(Reset), .Q(_1_Scatto_R__2_Fatto_q));  // open: Qn, preset, reset, en
  Counter #(.width(3), .max('h7)) counter_3 (
    .Q(Posizione_R_3), .clk(multiplexer_3_out), .clr(or_3_out));  // open: load, D, count, carry
  or or_3 (or_3_out, verifica_posizione_rotore_3_da_ritornare_a_0, Reset);
  Multiplexer multiplexer_3 (
    .in0(Input_Pos__3), .in1(and_2_out), .out(multiplexer_3_out), .sel(Setting_Concluso));  // open: en
  and and_2 (and_2_out, verifica_posizione_rotore_2_da_ritornare_a_0, Tastiera_Attivata, _1_Scatto_R__2_Fatto_q);
  Verifica_Posizione_Rotore verifica_posizione_rotore_3 (
    .in_1(Posizione_R_3), .Da_ritornare_a_0(verifica_posizione_rotore_3_da_ritornare_a_0));

  // Other names for the same wires on the sheet: bit_0_R1 = Posizione_R_1[0]; bit_0_R2 = Posizione_R_2[0]
endmodule

module Verifica_Posizione_Rotore (
  input  [2:0] in_1,
  output Da_ritornare_a_0
);

  and and_1 (Da_ritornare_a_0, in_1[0], in_1[1], in_1[2]);
endmodule

module Rotori (
  input  [2:0] Lettera_in_Input,
  input  [2:0] Posizione_Rotore_1,
  input  [2:0] Posizione_Rotore_3,
  input  [2:0] Posizione_Rotore_2,
  output [2:0] Lettera_in_Output
);

  wire not_0_1_out_2;
  wire [2:0] rotore_singolo_1_lettera_in_output, rotore_singolo_2_lettera_in_output,
       rotore_singolo_3_lettera_in_output;

  Not_0 not_0_1 (.in_1(Lettera_in_Input), .out_2(not_0_1_out_2));
  Rotore_Singolo rotore_singolo_1 (
    .in_2(Posizione_Rotore_1), .in_1(Lettera_in_Input), .Lettera_in_output(rotore_singolo_1_lettera_in_output));
  Rotore_Singolo rotore_singolo_2 (
    .in_2(Posizione_Rotore_2), .in_1(rotore_singolo_1_lettera_in_output),
    .Lettera_in_output(rotore_singolo_2_lettera_in_output));
  Rotore_Singolo rotore_singolo_3 (
    .in_2(Posizione_Rotore_3), .in_1(rotore_singolo_2_lettera_in_output),
    .Lettera_in_output(rotore_singolo_3_lettera_in_output));
  Multiplexer #(.width(3)) multiplexer_1 (
    .in0(Lettera_in_Input), .in1(rotore_singolo_3_lettera_in_output), .out(Lettera_in_Output),
    .sel(not_0_1_out_2));  // open: en
endmodule

module Rotore_Singolo (
  input  [2:0] in_1,
  input  [2:0] in_2,
  output [2:0] Lettera_in_output
);

  wire adder_1_cout;
  wire [2:0] adder_1_out, adder_2_out;

  Adder #(.width(3)) adder_1 (.a(in_1), .b(in_2), .out(adder_1_out), .cout(adder_1_cout));  // open: cin
  Adder #(.width(3)) adder_2 (.a(adder_1_out), .b(3'b001), .out(adder_2_out));  // open: cin, cout
  Multiplexer #(.width(3)) multiplexer_1 (
    .in0(adder_1_out), .in1(adder_2_out), .out(Lettera_in_output), .sel(adder_1_cout));  // open: en

  // Other names for the same wires on the sheet: Lettera[2:0] = in_1; Posizioni_Spostate[2:0] = in_2
endmodule

// Mem. Plug
module Memoria_PlugBoard (
  input  [2:0] Lettera_in_Input,
  input  Clock,
  input  Reset,
  output [2:0] Prima_Lettera_da_Sostituire,
  output [2:0] Prima_Lettera_in_Sostituzione,
  output [2:0] Seconda_Lettera_da_Sostituire,
  output [2:0] Seconda_Lettera_in_Sostituzione
);

  wire and_2_out, Attiva_Memoria_2, Attiva_Memoria_3, Attiva_Memoria_4, Memoria_1_Piena, Memoria_2_Piena,
       Memoria_3_Piena, Memoria_4_Piena, not_0_1_out_2, not_1_out, not_2_out, not_3_out, not_4_out;

  Not_0 not_0_1 (.in_1(Lettera_in_Input), .out_2(not_0_1_out_2));
  and and_1 (Attiva_Memoria_2, Memoria_1_Piena, not_0_1_out_2, not_1_out);
  not not_1 (not_1_out, Memoria_2_Piena);
  and and_2 (and_2_out, not_0_1_out_2, not_3_out);
  and and_3 (Attiva_Memoria_3, Memoria_2_Piena, not_0_1_out_2, not_2_out);
  not not_2 (not_2_out, Memoria_3_Piena);
  Register #(.width(3)) Memoria_1 (
    .D(Lettera_in_Input), .en(and_2_out), .Q(Prima_Lettera_da_Sostituire), .clk(Clock), .clr(Reset));
  not not_3 (not_3_out, Memoria_1_Piena);
  Register #(.width(3)) Memoria_2 (
    .D(Lettera_in_Input), .en(Attiva_Memoria_2), .Q(Prima_Lettera_in_Sostituzione), .clk(Clock), .clr(Reset));
  Register #(.width(3)) register_1 (
    .D(Lettera_in_Input), .en(Attiva_Memoria_3), .Q(Seconda_Lettera_da_Sostituire), .clk(Clock), .clr(Reset));
  Register #(.width(3)) register_2 (
    .D(Lettera_in_Input), .en(Attiva_Memoria_4), .Q(Seconda_Lettera_in_Sostituzione), .clk(Clock), .clr(Reset));
  Not_0 not_0_2 (.in_1(Prima_Lettera_da_Sostituire), .out_2(Memoria_1_Piena));
  Not_0 not_0_3 (.in_1(Prima_Lettera_in_Sostituzione), .out_2(Memoria_2_Piena));
  Not_0 not_0_4 (.in_1(Seconda_Lettera_da_Sostituire), .out_2(Memoria_3_Piena));
  Not_0 not_0_5 (.in_1(Seconda_Lettera_in_Sostituzione), .out_2(Memoria_4_Piena));
  and and_4 (Attiva_Memoria_4, Memoria_3_Piena, not_0_1_out_2, not_4_out);
  not not_4 (not_4_out, Memoria_4_Piena);
endmodule

module PlugBoard (
  input  [2:0] Seconda_Lettera_da_Sostituire,
  input  [2:0] Seconda_Lettera_in_Sostituzione,
  input  [2:0] Lettera_in_Input,
  input  [2:0] Prima_Lettera_da_Sostituire,
  input  [2:0] Prima_Lettera_in_Sostituzione,
  output [2:0] Output
);

  wire Primo_Plug_check_di_sotituzione_avvenuta;
  wire [2:0] Primo_Plug_output, Secondo_Plug_output;

  Plug_SIngolo Primo_Plug (
    .in_1(Lettera_in_Input), .in_2(Prima_Lettera_da_Sostituire), .in_3(Prima_Lettera_in_Sostituzione),
    .Output(Primo_Plug_output), .Check_di_Sotituzione_Avvenuta(Primo_Plug_check_di_sotituzione_avvenuta));
  Plug_SIngolo Secondo_Plug (
    .in_1(Lettera_in_Input), .in_2(Seconda_Lettera_da_Sostituire), .in_3(Seconda_Lettera_in_Sostituzione),
    .Output(Secondo_Plug_output));  // open: Check_di_Sotituzione_Avvenuta
  Multiplexer #(.width(3)) multiplexer_1 (
    .in0(Secondo_Plug_output), .in1(Primo_Plug_output), .out(Output),
    .sel(Primo_Plug_check_di_sotituzione_avvenuta));  // open: en
endmodule

module Plug_SIngolo (
  input  [2:0] in_1,
  input  [2:0] in_2,
  input  [2:0] in_3,
  output [2:0] Output,
  output Check_di_Sotituzione_Avvenuta
);

  Comparator #(.width(3)) comparator_1 (.a(in_1), .b(in_2), .eq(Check_di_Sotituzione_Avvenuta));  // open: gt, lt
  Multiplexer #(.width(3)) multiplexer_1 (
    .in0(in_1), .in1(in_3), .out(Output), .sel(Check_di_Sotituzione_Avvenuta));  // open: en

  // Other names for the same wires on the sheet: Input[2:0] = in_1; Lettera_da_Sostituire[2:0] = in_2;
  //   Output_Desiderato[2:0] = in_3
endmodule

// Mem. Lettera
module Ultima_Lettera_Inserita (
  input  [2:0] Lettera_in_Input,
  input  Clock,
  input  Reset,
  output [2:0] out_4
);

  wire not_0_1_out_2;

  Not_0 not_0_1 (.in_1(Lettera_in_Input), .out_2(not_0_1_out_2));
  Register #(.width(3)) register_1 (.D(Lettera_in_Input), .en(not_0_1_out_2), .Q(out_4), .clk(Clock), .clr(Reset));
endmodule

module Pulsantiera (
  input  in_1,
  input  in_2,
  input  in_3,
  input  in_4,
  input  in_5,
  input  in_6,
  input  in_7,
  output [2:0] out_8,
  output Pulsante_Premuto
);

  or or_1 (out_8[2], in_1, in_2, in_3, in_4);
  or or_2 (out_8[1], in_1, in_2, in_5, in_6);
  or or_3 (out_8[0], in_1, in_3, in_5, in_7);
  or or_4 (Pulsante_Premuto, out_8[2], out_8[1], out_8[0]);
endmodule

// L
module Convertitore_Led (
  input  [2:0] in_1,
  output [7:0] out_2
);

  Multiplexer #(.select(3), .width(8)) multiplexer_1 (
    .in1(8'h34), .in2(8'h1e), .in3(8'h6e), .in4(8'h77), .in5(8'h41), .in6(8'h3e), .in7(8'h5f), .out(out_2),
    .sel(in_1));  // open: in0, en
endmodule

module Not_0 (
  input  [2:0] in_1,
  output out_2
);

  or or_1 (out_2, in_1[0], in_1[1], in_1[2]);
endmodule
